// Logisim project HALF ADDER.circ as structural Verilog: 1 circuit, main circuit main
module main (
  input  A,
  input  B,
  output SUM,
  output CARRY
);

  wire xor_1_out;

  xor xor_1 (xor_1_out, A, B);
  and and_1 (CARRY, A, B);
endmodule
